// Logisim project part_1.circ as structural Verilog: 1 circuit, main circuit main
module main (
);

  wire and_1_out, and_2_out, clock_1_out, comparator_1_lt, comparator_2_eq, not_1_out;
  wire [15:0] adder_1_out, counter_1_q, counter_2_q, register_1_q, rom_1_data, shift_register_1_q0,
       shift_register_1_q1;

  Clock clock_1 (.out(clock_1_out));
  and and_1 (and_1_out, clock_1_out, comparator_1_lt);
  Counter #(.width(16), .max('h7dd), .trigger("falling")) counter_1 (
    .Q(counter_1_q), .clk(and_1_out));  // open: load, D, count, carry, clr
  Counter #(.width(16), .max('hffff), .trigger("falling")) counter_2 (
    .Q(counter_2_q), .clk(and_1_out));  // open: load, D, count, carry, clr
  Comparator #(.width(16)) comparator_1 (.a(counter_2_q), .b(16'h7df), .lt(comparator_1_lt));  // open: gt, eq
  not not_1 (not_1_out, and_1_out);
  ROM #(.addrWidth(16), .dataWidth(16)) rom_1 (.addr(counter_1_q), .data(rom_1_data));  // open: sel
  Shift_Register #(.width(16), .length(2)) shift_register_1 (
    .in(rom_1_data), .clk(and_1_out), .q0(shift_register_1_q0), .q1(shift_register_1_q1));  // open: shift, out, load, clr, d0, d1
  and and_2 (and_2_out, not_1_out, comparator_2_eq);
  Comparator #(.width(16)) comparator_2 (
    .a(shift_register_1_q1), .b(shift_register_1_q0), .eq(comparator_2_eq));  // open: gt, lt
  Adder #(.width(16)) adder_1 (.a(shift_register_1_q0), .b(register_1_q), .out(adder_1_out));  // open: cin, cout
  Register #(.width(16)) register_1 (.D(adder_1_out), .Q(register_1_q), .clk(and_2_out));  // open: en, clr

  // Notes on the sheet:
  //   contents of rom_1 (hex, n*v repeats v):
  //   3 2 9 4 1 9 9 4 7 1 3 2 7 1 9 5 9 9 4 8 2 4 8 3 2 1 9 7 5 6 4 8 5 9 8 7 6 6 8 2 6 3 8 1 4*8 9 7 6 8
  //   2 9 8 8 9 4 2 4 3 8 3 2 6 6 5 6 5 4 6 8 1 4 1 2 8 8 6 8 6 2 2 3 4 5 2 5 9 9 1 5 5 3 2 7 6 5 7 8 6 4
  //   1 2 6 5 5 8 9 9 5 9 1 7 8 4 1 4 2 1 8 3 8 9 3 2 9 3 6 1 4 9 6 6 7 3 9 9 1 6 1 4 6 7 3 6 2 6 3 4 4 5
  //   5 2 1 7 9 4 1 3 9 9 5 5 6 2 2 6 6 8 1 8 1 3 8 3 7 2 3 9 3 2 1 3 9 6 6 1 4 3 1 2 4 9 1 4 4 6 9 3 9 7
  //   6 9 2 5 8 7 2 5 1 1 1 2 6 6 3 2 1 7 8 6 2 8 7 9 2 3 3 2 2 6 7 6 3 5 3 3 9 1 1 1 2 8 8 9 3 3 5 4 5 3
  //   6 3 5 3 2 1 3 8 4 7 1 2 2 2 5 1 4 6 3 8 5 7 8 9 4 1 5 9 8 1 9 8 2 8 7 2 4 8 2 7 9 6 9 5 7 6 4 3 2 1
  //   9 1 8 4 7 7 8 7 7 7 2 7 3 2 8 8 1 2 6 6 8 7 5 4 6 9 7 2 1 1 8 9 3 3 1 8 8 2 2 2 8 1 4 6 5 7 6 8 3 2
  //   9 2 1 3 1 4 6 3 8 2 2 1 3 1 7 3 9 3 2 5 6 4 7 1 9 9 8 5 9 8 1 1 7 2 8 9 6 3 2 6 8 4 6 6 3 3 5 5 2 7
  //   3 8 4 5 9 8 3 9 3 3 8 4 5 7 2 1 7 1 3 4 9 7 8 1 1 7 6 6 9 9 5 3 6 7 7 9 5 8 5 7 9 6 5 2 2 2 1 8 3 6
  //   6 8 7 6 5 5 1 7 4 5 4 2 6 3 3 5 4 4*1 3 4 8 4 1 3 3 4 6 3 1 3 4 5 1 1 1 5 9 6 1 3 1 6 8 2 7 2 6 1 9
  //   6 5 7 4 7 6 3 1 6 5 1 8 7 8 8 9 3 3 7 5 9 9 5 8 3 3 4 5 6 3 4 4 1 3 4 3 6 1 6 5 5 3 9 7 4 4 1 8 8 8
  //   6 6 1 5 6 7 7 1 5 8 5 6 4 7 7 1 8 5 5 5 1 8 2 5 2 9 9 3 6 6 6 9 6 8 3 5 8 1 6 6 2 3 9 8 6 1 8 7 6 5
  //   3 9 1 4 8 7 1 6 4 7 1 5 7 2 4 8 4 9 8 9 4 5 6 3 3 1 4 4 2 6 9 5 9 3 4 8 1 1 9 2 8 6 9 5 5 1 4 4 4 3
  //   9 4 5 2 7 3 1 7 6 2 6 6 6 5 6 8 7 4 1 6 1 2 1 5 3 2 5 4 4 6 9 1 3 1 7 2 4 1 3 7 6 9 9 8 3 2 9 8 4 7
  //   2 8 9 3 7 8 6 5 9 5 6 7 1 1 9 2 5 5 9 2 6 2 8 4 5 6 6 1 7 1 3 3 6 9 5 2 5 9 5 5 4 5 4 8 7 1 9 3 2 8
  //   2 2 9 9 3 8 6 2 1 3 3 2 3 2 5 1 2 5 9 7 2 5 4 7 1 8 1 2 3 6 8 1 2 2 6 3 8 8 7 3 7 5 8 6 6 2 3 1 1 1
  //   8 3 1 2 9 5 4 3 6 9 4 3 2 9 3 7 3 5 9 3 5 7 2 6 6 4 6 7 3 8 3 3 1 8 3 2 6 2 3 9 5 7 2 8 7 7 3 1 4 7
  //   6 5 1 2 1 8 4 4 8 3 1 1 2 6 1 7 8 1 7 3 9 8 8 7 9 9 7 6 5 2 1 8 9 1 3 1 7 8 8 2 5 9 6 6 2 6 8 8 1 6
  //   4 7 6 5 5 9 7 9 2 9 4 7 3 5 9 9 5 6 8 5 9 9 8 9 2 2 8 9 1 7 1 3 6 2 6 7 1 7 8 5 7 1 7 7 6 3 1 6 3 4
  //   5 2 9 2 5 7 3 4 8 9 8 7 3 7 9 2 1 4 9 6 4 6 5 4 8 7 4 7 9 9 5 3 8 9 6 6 9 6 9 2 1 8 8 4 5 7 7 2 4 4
  //   1 4 4 6 8 7 2 7 1 9 2 8 1 9 9 1 9 4 4 8 2 7 5 9 2 2 1 6 6 3 2 1 1 5 8 1 4 1 3 6 5 2 3 7 5 4 5 2 2 2
  //   6 3 3 6 8 8 3 7 2 8 9 1 4 5 1 8 4 2 4 3 4 4 5 8 5 2 7 6 9 8 7 7 4 3 4 2 1 1 1 4 8 2 4 9 8 9 9 9 3 8
  //   3 8 3 1 4 9 2 5 7 7 6 1 5 1 5 4 5 9 1 2 7 8 7 1 9 6 5 6 7 9 8 2 7 7 3 7 7 3 6 3 2 8 4 3 7 9 4 6 8 7
  //   5 7 9 9 8 3 7 3 1 9 3 2 3 1 7 9 5 7 6 7 6 4 4 6 5 4 1 5 5 4 3 2 6 9 2 9 8 8 6 5 1 3 1 2 8 4 5 4 3 3
  //   5 1 1 8 7 9 4 5 7 9 2 1 6 3 8 9 3 4 8 7 7 5 5 7 5 7 5 2 4 1 3 9 4 3 6 3 7 2 1 6 6 7 2 3 7 7 7 8 9 6
  //   2 4 5 5 9 6 1 4 9 3 5 5 9 8 4 8 5 2 2 5 8 2 4 1 3 7 4 8 2 1 8 9 7 1 2 1 2 4 8 6 3 7 3 2 3 2 7 9 5 8
  //   7 8 3 6 2 9 6 4 8 7 3 8 5 5 9 9 4 6 9 7 1 4 9 6 9 2 8 2 4 9 1 7 1 8 3 3 7 5 5 4 5 1 9 2 1 1 9 4 5 3
  //   5 8 7 3 9 8 1 9 9 9 1 2 5 6 4 4 7 4 6 1 4 2 1 9 9 2 9 3 4 5 1 8 5 4 6 8 6 6 1 1 2 9 9 6 6 3 7 9 6 9
  //   3 8 1 3 4 9 8 5 4 2 4 7 4 7 3 2 1 9 8 1 7 6 4 9 6 6 9 4 7 4 6 1 1 1 5 7 6 9 2 5 7 1 5 4 9 3 9 6 7 2
  //   9 6 4 8 7 2 5 8 2 3 7 8 5 4 1 5 2 3 8 2 3 6 5 5 7 9 8 7 6 8 9 4 3 9 1 8 1 5 7 5 9 8 1 5 3 7 3 3 1 9
  //   1 5 9 2 1 3 4 7 4*5 2 5 1 4 8 8 7 5 4 2 7 9 8 8 8 2 4 5 4 9 2 3 7 3 5 9 5 4 7 1 1 8 9 1 9 1 3 5 3 2
  //   4 4 6 8 4 6 9 7 6 6 2 8 4 8 3 7 6 5 2 9 8 8 1 5 1 2 5 2 9 2 2 1 6 2 7 3 1 3 5 2 7 4 4 1 2 2 1 4 5 9
  //   6 7 2 7 8 6 9 2 3 1 4 5 1 6 5 9 8 9 6 1 1 2 2 3 3 7 2 2 4 1 1 4 9 9 2 9 4 3 6 2 4 7 3 7 4 8 1 8 4 6
  //   7 4 8 1 6 4 1 9 3 1 8 7 2 9 7 2 5 8 2 2 9 5 4 2 5 9 3 6 9 9 8 5 3 5 1 9 4 4 2 3 9 1 6 5 4 4 3 6 7 7
  //   9 9 5 2 2 2 7 6 9 1 4 4 4 5 2 3 1 5 8 2 2 7 2 3 6 8 3 8 8 8 3 1 8 3 4 4 3 7 5 6 2 7 5 2 1 1 9 3 2 5
  //   2 8 6 4 7 4 3 5 2 8 6 3 5 5 4 6 9 3 3 7 3 7 1 8 8 4 8 6 4 9 5 6 8 4 5 1 7 9 7 7 5 1 9 2 6 3 1 5 6 1
  //   7 5 7 5 2 9 5 3 8 1 9 6 4 4 2 6 8 4 3 6 2 5 2 8 2 8 1 9 5 2 4 7 4 7 1 1 9 7 2 6 8 7 2 1 9 3 5 6 9 7
  //   8 5 6 1 1 9 5 9 8 9 6 7 7 6 1 4 3 5 3 9 9 1 5 2 9 9 9 6 8 2 7 6 3 7 4 7 1 2 9 9 6 4 8 5 3 6 7 8 5 3
  //   4 9 4 7 3 4 3 7 6 2 5 7 5 1 1 2 7 3 4 4 3 7 3 6 4 3 3 4 6 4 4 9 6 2 8 7 2 1 9 6 1 5 6 9 7 3 4 1 9 7
  //   3 1 3 1 7 1 5 1 6 6 7 6 8 9 1 6 1 4 9 8 2 8 3 9 6 4 5 4 6 3 8 5 9 6 7 1 3 5 7 2 9 6 3 6 8 6 1 5 9 2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
endmodule
